// Logisim project ejercicio1.circ as structural Verilog: 1 circuit, main circuit main
module main (
  input  A,
  input  A_2,
  input  B,
  input  B_2,
  input  A_3,
  input  B_3,
  input  A_4,
  output implicacion,
  output XOR,
  output negacion,
  output \or 
);

  wire transistor_1_out, transistor_3_out, transistor_8_out;

  Transistor transistor_1 (.in(1'b1), .out(transistor_1_out), .gate(A));
  Pull_Resistor pull_resistor_1 (.node(transistor_1_out));
  Transistor #(.\type ("n")) transistor_2 (.in(transistor_1_out), .out(XOR), .gate(B_2));
  Transistor transistor_3 (.in(1'b1), .out(transistor_3_out), .gate(B_2));
  Pull_Resistor pull_resistor_2 (.node(transistor_3_out));
  Transistor transistor_4 (.in(1'b1), .out(negacion), .gate(A_3));
  Transistor #(.\type ("n")) transistor_5 (.in(A), .out(XOR), .gate(transistor_3_out));
  Pull_Resistor pull_resistor_3 (.node(negacion));
  Transistor #(.\type ("n")) transistor_6 (.in(1'b1), .out(\or ), .gate(A_4));
  Pull_Resistor pull_resistor_4 (.node(\or ));
  Transistor #(.\type ("n")) transistor_7 (.in(1'b1), .out(\or ), .gate(B_3));
  Transistor transistor_8 (.in(1'b1), .out(transistor_8_out), .gate(A_2));
  Transistor #(.\type ("n")) transistor_9 (.in(1'b1), .out(implicacion), .gate(transistor_8_out));
  Pull_Resistor pull_resistor_5 (.node(transistor_8_out));
  Pull_Resistor pull_resistor_6 (.node(implicacion));
  Transistor #(.\type ("n")) transistor_10 (.in(1'b1), .out(implicacion), .gate(B));

  // Notes on the sheet:
  //   NOT
  //   circuito XOR
  //   requisito para poder utilizar XOR en el ejercicio 2
  //   Dania Paula Góngora Ramírez 9.1
  //   OR
  //   implicación
endmodule
