// Logisim project ejercicio2.circ as structural Verilog: 1 circuit, main circuit main
module main (
  input  A_1,
  input  A_0,
  input  B_1,
  input  B_0,
  output x_y,
  output x_y_2,
  output x_y_3
);

  wire and_1_out, and_2_out, and_3_out, and_4_out, and_5_out, and_6_out, and_8_out, not_1_out, not_2_out,
       not_3_out, not_4_out, not_5_out, not_6_out, or_2_out, xor_1_out, xor_2_out;

  not not_1 (not_1_out, A_1);
  not not_2 (not_2_out, A_0);
  not not_3 (not_3_out, B_1);
  not not_4 (not_4_out, B_0);
  xor xor_1 (xor_1_out, A_1, B_1);
  xor xor_2 (xor_2_out, A_0, B_0);
  and and_1 (and_1_out, not_1_out, B_1);
  and and_2 (and_2_out, not_2_out, B_1, B_0);
  and and_3 (and_3_out, not_1_out, not_2_out, B_0);
  and and_4 (and_4_out, A_1, not_3_out);
  and and_5 (and_5_out, A_0, not_4_out);
  and and_6 (and_6_out, A_1, A_0);
  not not_5 (not_5_out, xor_1_out);
  not not_6 (not_6_out, xor_2_out);
  or or_1 (x_y_2, and_1_out, and_2_out, and_3_out);
  or or_2 (or_2_out, and_5_out, and_6_out);
  and and_7 (x_y, not_5_out, not_6_out);
  and and_8 (and_8_out, or_2_out, B_0);
  or or_3 (x_y_3, and_4_out, and_8_out);

  // Notes on the sheet:
  //   Dania Paula Gongora Ramirez Ejercicio 9.2
  //   x=y
  //   x < y
  //   x>y
endmodule
