// Logisim project sumador.circ as structural Verilog: 11 circuits, main circuit main
module main (
  input  x,
  input  y,
  input  c,
  output s,
  output s_acarreo
);

  wire and_1_out, and_2_out, xor_1_out;

  xor xor_1 (xor_1_out, x, y);
  and and_1 (and_1_out, xor_1_out, c);
  and and_2 (and_2_out, x, y);
  or or_1 (s_acarreo, and_1_out, and_2_out);
  xor xor_2 (s, xor_1_out, c);
endmodule

module sumador_8_bits (
  input  [7:0] x,
  input  [7:0] y,
  output desborde,
  output [7:0] suma
);

  wire sumador_1_bit_1_s_acarreo, sumador_1_bit_2_s_acarreo, sumador_1_bit_3_s_acarreo,
       sumador_1_bit_4_s_acarreo, sumador_1_bit_5_s_acarreo, sumador_1_bit_6_s_acarreo,
       sumador_1_bit_7_s_acarreo;

  sumador_1_bit sumador_1_bit_1 (.x(x[0]), .y(y[0]), .c(1'b0), .s(suma[0]), .s_acarreo(sumador_1_bit_1_s_acarreo));
  sumador_1_bit sumador_1_bit_2 (
    .x(x[1]), .y(y[1]), .c(sumador_1_bit_1_s_acarreo), .s(suma[1]), .s_acarreo(sumador_1_bit_2_s_acarreo));
  sumador_1_bit sumador_1_bit_3 (
    .x(x[2]), .y(y[2]), .c(sumador_1_bit_2_s_acarreo), .s(suma[2]), .s_acarreo(sumador_1_bit_3_s_acarreo));
  sumador_1_bit sumador_1_bit_4 (
    .x(x[3]), .y(y[3]), .c(sumador_1_bit_3_s_acarreo), .s(suma[3]), .s_acarreo(sumador_1_bit_4_s_acarreo));
  sumador_1_bit sumador_1_bit_5 (
    .x(x[4]), .y(y[4]), .c(sumador_1_bit_4_s_acarreo), .s(suma[4]), .s_acarreo(sumador_1_bit_5_s_acarreo));
  sumador_1_bit sumador_1_bit_6 (
    .x(x[5]), .y(y[5]), .c(sumador_1_bit_5_s_acarreo), .s(suma[5]), .s_acarreo(sumador_1_bit_6_s_acarreo));
  sumador_1_bit sumador_1_bit_7 (
    .x(x[6]), .y(y[6]), .c(sumador_1_bit_6_s_acarreo), .s(suma[6]), .s_acarreo(sumador_1_bit_7_s_acarreo));
  sumador_1_bit sumador_1_bit_8 (.x(x[7]), .y(y[7]), .c(sumador_1_bit_7_s_acarreo), .s(suma[7]), .s_acarreo(desborde));
endmodule

module sumador_1_bit (
  input  x,
  input  y,
  input  c,
  output s,
  output s_acarreo
);

  wire and_1_out, and_2_out, xor_1_out;

  xor xor_1 (xor_1_out, x, y);
  and and_1 (and_1_out, xor_1_out, c);
  and and_2 (and_2_out, x, y);
  or or_1 (s_acarreo, and_1_out, and_2_out);
  xor xor_2 (s, xor_1_out, c);
endmodule

module and_1_bit (
  input  x,
  input  y,
  output s
);

  and and_1 (s, x, y);
endmodule

module and_8_bits (
  input  [7:0] x,
  input  [7:0] y,
  output [7:0] s
);

  and_1_bit and_1_bit_1 (.x(x[0]), .y(y[0]), .s(s[0]));
  and_1_bit and_1_bit_2 (.x(x[1]), .y(y[1]), .s(s[1]));
  and_1_bit and_1_bit_3 (.x(x[2]), .y(y[2]), .s(s[2]));
  and_1_bit and_1_bit_4 (.x(x[3]), .y(y[3]), .s(s[3]));
  and_1_bit and_1_bit_5 (.x(x[4]), .y(y[4]), .s(s[4]));
  and_1_bit and_1_bit_6 (.x(x[5]), .y(y[5]), .s(s[5]));
  and_1_bit and_1_bit_7 (.x(x[6]), .y(y[6]), .s(s[6]));
  and_1_bit and_1_bit_8 (.x(x[7]), .y(y[7]), .s(s[7]));
endmodule

module or_8_b_its (
  input  [7:0] x,
  input  [7:0] y,
  output [7:0] s
);

  or or_1 (s[0], x[0], y[0]);
  or or_2 (s[1], x[1], y[1]);
  or or_3 (s[2], x[2], y[2]);
  or or_4 (s[3], x[3], y[3]);
  or or_5 (s[4], x[4], y[4]);
  or or_6 (s[5], x[5], y[5]);
  or or_7 (s[6], x[6], y[6]);
  or or_8 (s[7], x[7], y[7]);
endmodule

module restador_8_bits (
  input  [7:0] x,
  input  [7:0] y,
  output desborde,
  output [7:0] s
);

  wire [7:0] negador_8_bits_1_s, sumador_8_bits_1_suma;

  negador_8_bits negador_8_bits_1 (.x(y), .s(negador_8_bits_1_s));
  sumador_8_bits sumador_8_bits_1 (.x(x), .y(negador_8_bits_1_s), .suma(sumador_8_bits_1_suma));  // open: desborde
  sumador_8_bits sumador_8_bits_2 (.x(sumador_8_bits_1_suma), .y(8'h1), .desborde(desborde), .suma(s));

  // Notes on the sheet:
  //   complemento
  //   sumador
  //   sumador
endmodule

module negador_8_bits (
  input  [7:0] x,
  output [7:0] s
);

  not not_1 (s[0], x[0]);
  not not_2 (s[1], x[1]);
  not not_3 (s[2], x[2]);
  not not_4 (s[3], x[3]);
  not not_5 (s[4], x[4]);
  not not_6 (s[5], x[5]);
  not not_7 (s[6], x[6]);
  not not_8 (s[7], x[7]);
endmodule

module \comparación  (
  input  [7:0] x,
  input  [7:0] y,
  output desborde,
  output [7:0] out_4,
  output x_y
);

  restador_8_bits restador_8_bits_1 (.x(x), .y(y), .desborde(desborde), .s(out_4));

  assign x_y = out_4[7];
endmodule

module ALU (
  input  [7:0] x,
  input  [7:0] y,
  output out_3,
  output [7:0] out_4,
  output [7:0] out_5,
  output [7:0] out_6,
  output out_7,
  output [7:0] out_8,
  output out_9,
  output out_10
);

  sumador_8_bits sumador_8_bits_1 (.x(x), .y(y), .desborde(out_3), .suma(out_4));
  and_8_bits and_8_bits_1 (.x(x), .y(y), .s(out_5));
  or_8_b_its or_8_b_its_1 (.x(x), .y(y), .s(out_6));
  restador_8_bits restador_8_bits_1 (.x(x), .y(y), .desborde(out_7), .s(out_8));
  \comparación  \comparación_1  (.x(x), .y(y), .desborde(out_9), .x_y(out_10));  // open: out_4

  // Notes on the sheet:
  //   sumador
  //   and
  //   or
  //   restador
  //   comparador
endmodule

module igualar (
  input  [7:0] in_1,
  input  [7:0] in_2,
  output [7:0] out_3
);

  restador_8_bits restador_8_bits_1 (.x(in_1), .y(in_2), .s(out_3));  // open: desborde
endmodule
